# Fritzing sketch retic-controller (saved by Fritzing 1.0.2b)

parts:
  WeMos_D1_Mini1 = WeMos D1 Mini
  U1 = Module 4 Relais 5V [package="Module 4 Relais 5V"]
  Mod1 = KY-019 5V Relay Module [package="Breakout board"]
  D1 = Diode [package=diode-1n4148]
  D2 = Diode [package=diode-1n4148]
  D3 = Diode [package=diode-1n4148]
  D4 = Diode [package=diode-1n4148]
  S1 = Momentary Switch 6mm 2pin
  S2 = Momentary Switch 6mm 2pin
  S3 = Square Pushbutton
  R2 = Resistor [tolerance=±5% resistance=10k package="0805 [SMD]"]
  R3 = Resistor [tolerance=±5% resistance=10k package="0805 [SMD]"]
  R4 = Resistor [tolerance=±5% resistance=10k package="0805 [SMD]"]
  LED1 = smd LED [color="White (4500K)" package="0805 [SMD]"]
  F1 = FUSE [mn=2A package=fuse_5mm]

nets:
  N1: WeMos_D1_Mini1.3V3, R2.Pin_0, R3.Pin_0, R4.Pin_0
  5V: WeMos_D1_Mini1.5V, U1.VCC, Mod1.+
  N2: WeMos_D1_Mini1.D1, S3.leg0, R2.Pin_1
  N3: WeMos_D1_Mini1.D2, S1.1, R4.Pin_1
  N4: WeMos_D1_Mini1.D3, S2.1, R3.Pin_1
  N5: WeMos_D1_Mini1.D5, U1.IN1, D4.A
  N6: WeMos_D1_Mini1.D6, U1.IN2, D1.A
  N7: WeMos_D1_Mini1.D7, U1.IN3, D3.A
  N8: WeMos_D1_Mini1.D8, U1.IN4, D2.A
  N9: WeMos_D1_Mini1.G, U1.GND, Mod1.-, S1.2, S2.2, S3.leg1, LED1.cathode
  N10: U1.K1-NO, U1.K2-NO, U1.K3-NO, U1.K4-NO, Mod1.NO, F1.1
  N11: Mod1.S, D1.C, D2.C, D3.C, D4.C, LED1.anode

notes:
  Station 1
  Station 2
  Station 3
  Station 4
  Motor Relay
  24 VAC
  Motor Relay Ground
  Solenoid Ground
  5V USB
  Power Switch
  Start / Next Station
  Cancel

custom parts:
  WeMos D1 Mini: The D1 mini is a mini wifi board based on ESP-8266EX.
  Module 4 Relais 5V: Module 4 Relais 5V 4x SPD-06VDC-SD-C
  KY-019 5V Relay Module: KY-019 5V Relay module, used to control AC circuits. (Special thanks to vanepp for fixing the PCB holes and other errors)
  Momentary Switch 6mm 2pin: Momentary Switch 6mm 2 pin Button commonly used for reset or general input.
